# Fritzing sketch RaspiRemote (saved by Fritzing 0.9.9b)
circuit board: 8.46667cm x 5.64444cm
breadboards: 1

parts:
  TRRS = TRRS 3.5mm Jack Breakout
  U1 = Sharp PC817 [package=THT]
  U2 = Sharp PC817 [package=THT]
  R1 = Resistor [tolerance=±5% power=0.25 resistance=47 package=THT]
  R2 = Resistor [tolerance=±5% power=0.25 resistance=47 package=THT]
  MCU1 = Raspberry Pi Zero

nets:
  N1: TRRS.SLEEVE, U1.Pin_4, U2.Pin_4
  N2: TRRS.RING1, U2.Pin_3
  N3: TRRS.TIP, U1.Pin_3
  N4: U1.Pin_1, R2.Pin_1
  N5: U1.Pin_2, U2.Pin_2, MCU1.pin_6, MCU1.pin_9, MCU1.pin_25, MCU1.pin_39
  N6: U2.Pin_1, R1.Pin_1
  N7: R1.Pin_0, MCU1.pin_26
  N8: R2.Pin_0, MCU1.pin_35
